// Digital circuit Simplic-Refactor.dig as structural Verilog
module Simplic_Refactor (
);

  wire undriven_128;
  wire [0:0] demultiplexer_1_out_0;
  wire [3:0] undriven_130, undriven_131, undriven_132;
  wire [15:0] Addr_2_q, Addr_q, BUF_q, demultiplexer_1_out_1, demultiplexer_1_out_2, demultiplexer_1_out_3,
       demultiplexer_1_out_5, demultiplexer_1_out_6, demultiplexer_1_out_7, demultiplexer_1_out_9,
       demultiplexer_1_out_10, demultiplexer_1_out_11, demultiplexer_1_out_13, demultiplexer_1_out_14,
       demultiplexer_1_out_15, demultiplexer_2_out_0, demultiplexer_2_out_1, demultiplexer_2_out_2,
       demultiplexer_2_out_3, demultiplexer_2_out_4, demultiplexer_2_out_5, demultiplexer_2_out_6,
       demultiplexer_2_out_7, demultiplexer_2_out_8, demultiplexer_2_out_9, demultiplexer_2_out_10,
       demultiplexer_2_out_11, demultiplexer_2_out_12, demultiplexer_2_out_13, demultiplexer_2_out_14,
       demultiplexer_2_out_15, demultiplexer_3_out_0, demultiplexer_3_out_1, demultiplexer_3_out_2,
       demultiplexer_3_out_3, demultiplexer_3_out_4, demultiplexer_3_out_5, demultiplexer_3_out_6,
       demultiplexer_3_out_7, demultiplexer_3_out_8, demultiplexer_3_out_9, demultiplexer_3_out_10,
       demultiplexer_3_out_11, demultiplexer_3_out_12, demultiplexer_3_out_13, demultiplexer_3_out_14,
       demultiplexer_3_out_15, Link_q, PC_2_out, PC_3_out, PC_4_out, PC_out, R1_q, R2_q, R3_q, R4_q, R5_q,
       R6_q, R7_q, R8_q, R9_q, registerfile_1_da, registerfile_1_db, RET_q, STA_q, t1_q, t3_q, t5_q, t7_q,
       t8_q, t9_q, t10_q, t11_q, t12_q, t13_q, t14_q, t15_q, t17_q, t19_q, t21_q, t22_q, t23_q, t24_q, t25_q,
       t26_q, t27_q, t28_q, undriven, undriven_2, undriven_3, undriven_4, undriven_5, undriven_6, undriven_7,
       undriven_8, undriven_9, undriven_10, undriven_11, undriven_12, undriven_13, undriven_14, undriven_15,
       undriven_16, undriven_17, undriven_18, undriven_21, undriven_22, undriven_23, undriven_24,
       undriven_25, undriven_26, undriven_27, undriven_28, undriven_35, undriven_36, undriven_61,
       undriven_62, undriven_63, undriven_64, undriven_66, undriven_67, undriven_68, undriven_69,
       undriven_70, undriven_71, undriven_72, undriven_73, undriven_81, undriven_106, undriven_107,
       undriven_108, undriven_109, undriven_110, undriven_111, undriven_112, undriven_113, undriven_114,
       undriven_115, undriven_116, undriven_117, undriven_118, undriven_119, undriven_120, undriven_121,
       undriven_122, undriven_123, undriven_124, undriven_125, undriven_126, undriven_127, undriven_129;
  wire [15:1] demultiplexer_1_out_0_2, demultiplexer_1_out_4, demultiplexer_1_out_8, demultiplexer_1_out_12,
       t2_q, t4_q, t6_q, t16_q, t18_q, t20_q, undriven_19, undriven_20, undriven_29, undriven_30,
       undriven_31, undriven_32, undriven_33, undriven_34, undriven_37, undriven_38, undriven_39,
       undriven_40, undriven_41, undriven_42, undriven_43, undriven_44, undriven_45, undriven_46,
       undriven_47, undriven_48, undriven_49, undriven_50, undriven_51, undriven_52, undriven_53,
       undriven_54, undriven_55, undriven_56, undriven_57, undriven_58, undriven_59, undriven_60,
       undriven_65, undriven_74, undriven_75, undriven_76, undriven_77, undriven_78, undriven_79,
       undriven_80, undriven_82, undriven_83, undriven_84, undriven_85, undriven_86, undriven_87,
       undriven_88, undriven_89, undriven_90, undriven_91, undriven_92, undriven_93, undriven_94,
       undriven_95, undriven_96, undriven_97, undriven_98, undriven_99, undriven_100, undriven_101,
       undriven_102, undriven_103, undriven_104, undriven_105;

  RegisterFile #(.AddrBits(4), .Bits(16)) registerfile_1 (
    .Din(undriven_129), .we(1'b1), .Rw(undriven_130), .C(undriven_128), .Ra(undriven_131), .Rb(undriven_132),
    .Da(registerfile_1_da), .Db(registerfile_1_db));
  Register #(.Bits(16)) Addr (.Q(Addr_q));  // open: D, C, en
  CounterPreset #(.Bits(16)) PC (.out(PC_out));  // open: en, C, dir, in, ld, clr, ovf
  Demultiplexer #(.Selector_Bits(4), .Bits(16)) demultiplexer_1 (
    .out_0({demultiplexer_1_out_0_2, demultiplexer_1_out_0[0]}), .out_1(demultiplexer_1_out_1),
    .out_2(demultiplexer_1_out_2), .out_3(demultiplexer_1_out_3),
    .out_4({demultiplexer_1_out_4, undriven_116[0]}), .out_5(demultiplexer_1_out_5),
    .out_6(demultiplexer_1_out_6), .out_7(demultiplexer_1_out_7),
    .out_8({demultiplexer_1_out_8, undriven_120[0]}), .out_9(demultiplexer_1_out_9),
    .out_10(demultiplexer_1_out_10), .out_11(demultiplexer_1_out_11),
    .out_12({demultiplexer_1_out_12, undriven_124[0]}), .out_13(demultiplexer_1_out_13),
    .out_14(demultiplexer_1_out_14), .out_15(demultiplexer_1_out_15));  // open: sel, in
  Demultiplexer #(.Selector_Bits(4), .Bits(16)) demultiplexer_2 (
    .out_0(demultiplexer_2_out_0), .out_1(demultiplexer_2_out_1), .out_2(demultiplexer_2_out_2),
    .out_3(demultiplexer_2_out_3), .out_4(demultiplexer_2_out_4), .out_5(demultiplexer_2_out_5),
    .out_6(demultiplexer_2_out_6), .out_7(demultiplexer_2_out_7), .out_8(demultiplexer_2_out_8),
    .out_9(demultiplexer_2_out_9), .out_10(demultiplexer_2_out_10), .out_11(demultiplexer_2_out_11),
    .out_12(demultiplexer_2_out_12), .out_13(demultiplexer_2_out_13), .out_14(demultiplexer_2_out_14),
    .out_15(demultiplexer_2_out_15));  // open: sel, in
  Register #(.Bits(16)) t15 (.D(undriven_114), .Q(t15_q));  // open: C, en
  Register #(.Bits(16)) t16 (.D(undriven_116), .Q({t16_q, undriven_69[0]}));  // open: C, en
  Register #(.Bits(16)) t17 (.D(undriven_118), .Q(t17_q));  // open: C, en
  Register #(.Bits(16)) t18 (.D(undriven_120), .Q({t18_q, undriven_73[0]}));  // open: C, en
  Register #(.Bits(16)) t19 (.D(undriven_122), .Q(t19_q));  // open: C, en
  Register #(.Bits(16)) t20 (.D(undriven_124), .Q({t20_q, undriven_109[0]}));  // open: C, en
  Register #(.Bits(16)) t21 (.D(undriven_126), .Q(t21_q));  // open: C, en
  Register #(.Bits(16)) t22 (.D(undriven_113), .Q(t22_q));  // open: C, en
  Register #(.Bits(16)) t23 (.D(undriven_115), .Q(t23_q));  // open: C, en
  Register #(.Bits(16)) t24 (.D(undriven_117), .Q(t24_q));  // open: C, en
  Register #(.Bits(16)) t25 (.D(undriven_119), .Q(t25_q));  // open: C, en
  Register #(.Bits(16)) t26 (.D(undriven_121), .Q(t26_q));  // open: C, en
  Register #(.Bits(16)) t27 (.D(undriven_123), .Q(t27_q));  // open: C, en
  Register #(.Bits(16)) t28 (.D(undriven_125), .Q(t28_q));  // open: C, en
  CounterPreset #(.Bits(16)) PC_2 (
    .en(1'b1), .dir(1'b0), .in(undriven_127), .clr(1'b0), .out(PC_2_out));  // open: C, ld, ovf
  Register #(.Bits(16)) R2 (.D(demultiplexer_2_out_2), .Q(R2_q));  // open: C, en
  Register #(.Bits(16)) R4 (.D(demultiplexer_2_out_4), .Q(R4_q));  // open: C, en
  Register #(.Bits(16)) R6 (.D(demultiplexer_2_out_6), .Q(R6_q));  // open: C, en
  Register #(.Bits(16)) R8 (.D(demultiplexer_2_out_8), .Q(R8_q));  // open: C, en
  Register #(.Bits(16)) BUF (.D(demultiplexer_2_out_10), .Q(BUF_q));  // open: C, en
  Register #(.Bits(16)) STA (.D(demultiplexer_2_out_12), .Q(STA_q));  // open: C, en
  Register #(.Bits(16)) Link (.D(demultiplexer_2_out_14), .Q(Link_q));  // open: C, en
  Multiplexer #(.Selector_Bits(4), .Bits(16)) multiplexer_1 (
    .in_0({undriven_65, undriven_81[0]}), .in_1(undriven_66), .in_2(undriven_67), .in_3(undriven_68),
    .in_4(undriven_69), .in_5(undriven_70), .in_6(undriven_71), .in_7(undriven_72), .in_8(undriven_73),
    .in_9({undriven_74, undriven_106[0]}), .in_10({undriven_75, undriven_107[0]}),
    .in_11({undriven_76, undriven_108[0]}), .in_12({undriven_77, undriven_109[0]}),
    .in_13({undriven_78, undriven_110[0]}), .in_14({undriven_79, undriven_111[0]}),
    .in_15({undriven_80, undriven_112[0]}));  // open: sel, out
  Multiplexer #(.Selector_Bits(4), .Bits(16)) multiplexer_2 (
    .in_0(undriven_81), .in_1({undriven_82, undriven_66[0]}), .in_2({undriven_83, undriven_67[0]}),
    .in_3({undriven_84, undriven_68[0]}), .in_4({undriven_85, undriven_69[0]}),
    .in_5({undriven_86, undriven_70[0]}), .in_6({undriven_87, undriven_71[0]}),
    .in_7({undriven_88, undriven_72[0]}), .in_8({undriven_89, undriven_73[0]}),
    .in_9({undriven_90, undriven_106[0]}), .in_10({undriven_91, undriven_107[0]}),
    .in_11({undriven_92, undriven_108[0]}), .in_12({undriven_93, undriven_109[0]}),
    .in_13({undriven_94, undriven_110[0]}), .in_14({undriven_95, undriven_111[0]}),
    .in_15({undriven_96, undriven_112[0]}));  // open: sel, out
  Multiplexer #(.Selector_Bits(4), .Bits(16)) multiplexer_3 (
    .in_0({undriven_97, undriven_81[0]}), .in_1({undriven_98, undriven_66[0]}),
    .in_2({undriven_99, undriven_67[0]}), .in_3({undriven_100, undriven_68[0]}),
    .in_4({undriven_101, undriven_69[0]}), .in_5({undriven_102, undriven_70[0]}),
    .in_6({undriven_103, undriven_71[0]}), .in_7({undriven_104, undriven_72[0]}),
    .in_8({undriven_105, undriven_73[0]}), .in_9(undriven_106), .in_10(undriven_107), .in_11(undriven_108),
    .in_12(undriven_109), .in_13(undriven_110), .in_14(undriven_111), .in_15(undriven_112));  // open: sel, out
  Register #(.Bits(16)) R1 (.D(demultiplexer_2_out_1), .Q(R1_q));  // open: C, en
  Register #(.Bits(16)) R3 (.D(demultiplexer_2_out_3), .Q(R3_q));  // open: C, en
  Register #(.Bits(16)) R5 (.D(demultiplexer_2_out_5), .Q(R5_q));  // open: C, en
  Register #(.Bits(16)) R7 (.D(demultiplexer_2_out_7), .Q(R7_q));  // open: C, en
  Register #(.Bits(16)) R9 (.D(demultiplexer_2_out_9), .Q(R9_q));  // open: C, en
  Register #(.Bits(16)) RET (.D(demultiplexer_2_out_11), .Q(RET_q));  // open: C, en
  Register #(.Bits(16)) Addr_2 (.D(demultiplexer_2_out_13), .Q(Addr_2_q));  // open: C, en
  CounterPreset #(.Bits(16)) PC_3 (
    .en(1'b1), .dir(1'b0), .in(demultiplexer_2_out_15), .clr(1'b0), .out(PC_3_out));  // open: C, ld, ovf
  Demultiplexer #(.Bits(16), .Selector_Bits(4)) demultiplexer_3 (
    .out_0(demultiplexer_3_out_0), .out_1(demultiplexer_3_out_1), .out_2(demultiplexer_3_out_2),
    .out_3(demultiplexer_3_out_3), .out_4(demultiplexer_3_out_4), .out_5(demultiplexer_3_out_5),
    .out_6(demultiplexer_3_out_6), .out_7(demultiplexer_3_out_7), .out_8(demultiplexer_3_out_8),
    .out_9(demultiplexer_3_out_9), .out_10(demultiplexer_3_out_10), .out_11(demultiplexer_3_out_11),
    .out_12(demultiplexer_3_out_12), .out_13(demultiplexer_3_out_13), .out_14(demultiplexer_3_out_14),
    .out_15(demultiplexer_3_out_15));  // open: sel, in
  Multiplexer #(.Selector_Bits(4), .Bits(16)) multiplexer_4 (
    .in_0(demultiplexer_2_out_0), .in_1(R1_q), .in_2(R2_q), .in_3(R3_q), .in_4(R4_q), .in_5(R5_q),
    .in_6(R6_q), .in_7(R7_q), .in_8(R8_q), .in_9(R9_q), .in_10(BUF_q), .in_11(RET_q), .in_12(STA_q),
    .in_13(Addr_2_q), .in_14(Link_q), .in_15(PC_3_out));  // open: sel, out
  Multiplexer #(.Selector_Bits(4), .Bits(16)) multiplexer_5 (
    .in_0(demultiplexer_2_out_0), .in_1(R1_q), .in_2(R2_q), .in_3(R3_q), .in_4(R4_q), .in_5(R5_q),
    .in_6(R6_q), .in_7(R7_q), .in_8(R8_q), .in_9(R9_q), .in_10(BUF_q), .in_11(RET_q), .in_12(STA_q),
    .in_13(Addr_2_q), .in_14(Link_q), .in_15(PC_3_out));  // open: sel, out
  Multiplexer #(.Selector_Bits(4), .Bits(16)) multiplexer_6 (
    .in_0(demultiplexer_2_out_0), .in_1(R1_q), .in_2(R2_q), .in_3(R3_q), .in_4(R4_q), .in_5(R5_q),
    .in_6(R6_q), .in_7(R7_q), .in_8(R8_q), .in_9(R9_q), .in_10(BUF_q), .in_11(RET_q), .in_12(STA_q),
    .in_13(Addr_2_q), .in_14(Link_q), .in_15(PC_3_out));  // open: sel, out
  Register #(.Bits(16)) t1 (.D(demultiplexer_3_out_2), .Q(t1_q));  // open: C, en
  Register #(.Bits(16)) t2 (.D(demultiplexer_3_out_4), .Q({t2_q, undriven_21[0]}));  // open: C, en
  Register #(.Bits(16)) t3 (.D(demultiplexer_3_out_6), .Q(t3_q));  // open: C, en
  Register #(.Bits(16)) t4 (.D(demultiplexer_3_out_8), .Q({t4_q, undriven_25[0]}));  // open: C, en
  Register #(.Bits(16)) t5 (.D(demultiplexer_3_out_10), .Q(t5_q));  // open: C, en
  Register #(.Bits(16)) t6 (.D(demultiplexer_3_out_12), .Q({t6_q, undriven_61[0]}));  // open: C, en
  Register #(.Bits(16)) t7 (.D(demultiplexer_3_out_14), .Q(t7_q));  // open: C, en
  Register #(.Bits(16)) t8 (.D(demultiplexer_3_out_1), .Q(t8_q));  // open: C, en
  Register #(.Bits(16)) t9 (.D(demultiplexer_3_out_3), .Q(t9_q));  // open: C, en
  Register #(.Bits(16)) t10 (.D(demultiplexer_3_out_5), .Q(t10_q));  // open: C, en
  Register #(.Bits(16)) t11 (.D(demultiplexer_3_out_7), .Q(t11_q));  // open: C, en
  Register #(.Bits(16)) t12 (.D(demultiplexer_3_out_9), .Q(t12_q));  // open: C, en
  Register #(.Bits(16)) t13 (.D(demultiplexer_3_out_11), .Q(t13_q));  // open: C, en
  Register #(.Bits(16)) t14 (.D(demultiplexer_3_out_13), .Q(t14_q));  // open: C, en
  CounterPreset #(.Bits(16)) PC_4 (
    .en(1'b1), .dir(1'b0), .in(demultiplexer_3_out_15), .clr(1'b0), .out(PC_4_out));  // open: C, ld, ovf
  Multiplexer #(.Selector_Bits(4), .Bits(16)) multiplexer_7 (
    .in_0(undriven_17), .in_1(undriven_18), .in_2({undriven_19, undriven_35[0]}),
    .in_3({undriven_20, undriven_36[0]}), .in_4(undriven_21), .in_5(undriven_22), .in_6(undriven_23),
    .in_7(undriven_24), .in_8(undriven_25), .in_9(undriven_26), .in_10(undriven_27), .in_11(undriven_28),
    .in_12({undriven_29, undriven_61[0]}), .in_13({undriven_30, undriven_62[0]}),
    .in_14({undriven_31, undriven_63[0]}), .in_15({undriven_32, undriven_64[0]}));  // open: sel, out
  Multiplexer #(.Selector_Bits(4), .Bits(16)) multiplexer_8 (
    .in_0({undriven_33, undriven_17[0]}), .in_1({undriven_34, undriven_18[0]}), .in_2(undriven_35),
    .in_3(undriven_36), .in_4({undriven_37, undriven_21[0]}), .in_5({undriven_38, undriven_22[0]}),
    .in_6({undriven_39, undriven_23[0]}), .in_7({undriven_40, undriven_24[0]}),
    .in_8({undriven_41, undriven_25[0]}), .in_9({undriven_42, undriven_26[0]}),
    .in_10({undriven_43, undriven_27[0]}), .in_11({undriven_44, undriven_28[0]}),
    .in_12({undriven_45, undriven_61[0]}), .in_13({undriven_46, undriven_62[0]}),
    .in_14({undriven_47, undriven_63[0]}), .in_15({undriven_48, undriven_64[0]}));  // open: sel, out
  Multiplexer #(.Selector_Bits(4), .Bits(16)) multiplexer_9 (
    .in_0({undriven_49, undriven_17[0]}), .in_1({undriven_50, undriven_18[0]}),
    .in_2({undriven_51, undriven_35[0]}), .in_3({undriven_52, undriven_36[0]}),
    .in_4({undriven_53, undriven_21[0]}), .in_5({undriven_54, undriven_22[0]}),
    .in_6({undriven_55, undriven_23[0]}), .in_7({undriven_56, undriven_24[0]}),
    .in_8({undriven_57, undriven_25[0]}), .in_9({undriven_58, undriven_26[0]}),
    .in_10({undriven_59, undriven_27[0]}), .in_11({undriven_60, undriven_28[0]}), .in_12(undriven_61),
    .in_13(undriven_62), .in_14(undriven_63), .in_15(undriven_64));  // open: sel, out
  Multiplexer #(.Selector_Bits(4), .Bits(16)) multiplexer_10 (
    .in_0(undriven), .in_1(undriven_2), .in_2(undriven_3), .in_3(undriven_4), .in_4(undriven_5),
    .in_5(undriven_6), .in_6(undriven_7), .in_7(undriven_8), .in_8(undriven_9), .in_9(undriven_10),
    .in_10(undriven_11), .in_11(undriven_12), .in_12(undriven_13), .in_13(undriven_14), .in_14(undriven_15),
    .in_15(undriven_16));  // open: sel, out
  Multiplexer #(.Selector_Bits(4), .Bits(16)) multiplexer_11 (
    .in_0(undriven), .in_1(undriven_2), .in_2(undriven_3), .in_3(undriven_4), .in_4(undriven_5),
    .in_5(undriven_6), .in_6(undriven_7), .in_7(undriven_8), .in_8(undriven_9), .in_9(undriven_10),
    .in_10(undriven_11), .in_11(undriven_12), .in_12(undriven_13), .in_13(undriven_14), .in_14(undriven_15),
    .in_15(undriven_16));  // open: sel, out
  Multiplexer #(.Selector_Bits(4), .Bits(16)) multiplexer_12 (
    .in_0(undriven), .in_1(undriven_2), .in_2(undriven_3), .in_3(undriven_4), .in_4(undriven_5),
    .in_5(undriven_6), .in_6(undriven_7), .in_7(undriven_8), .in_8(undriven_9), .in_9(undriven_10),
    .in_10(undriven_11), .in_11(undriven_12), .in_12(undriven_13), .in_13(undriven_14), .in_14(undriven_15),
    .in_15(undriven_16));  // open: sel, out
  // Pins of 1 and 16 bits meet at undriven_17
  // Pins of 1 and 16 bits meet at undriven_18
  // Pins of 1 and 16 bits meet at {undriven_19, undriven_35[0]}
  // Pins of 1 and 16 bits meet at {undriven_20, undriven_36[0]}
  // Pins of 1 and 16 bits meet at undriven_21
  // Pins of 1 and 16 bits meet at undriven_22
  // Pins of 1 and 16 bits meet at undriven_23
  // Pins of 1 and 16 bits meet at undriven_24
  // Pins of 1 and 16 bits meet at undriven_25
  // Pins of 1 and 16 bits meet at undriven_26
  // Pins of 1 and 16 bits meet at undriven_27
  // Pins of 1 and 16 bits meet at undriven_28
endmodule
